# Fritzing sketch main (saved by Fritzing 0.9.10b)

parts:
  arduino = Arduino Nano (Rev3.0)
  bt = Bluetooth HC-06u [package=THT]
  5V->12V = Boost Convertor [part_number=XL6009E1 package=THT]
  5V = DC Power [voltage=5]
  water_pump = water pump/motor
  F1 = Fan - 4 wire [package=THT]

nets:
  N1: arduino.D5, F1.PWM
  N2: arduino.D7, bt.TXD
  N3: arduino.D8, bt.RXD
  GND: arduino.GND, bt.GND
  5V: arduino.5V, bt.VCC
  N4: arduino.A0, F1.Tach
  N5: 5V->12V.Negative_Input, 5V.V-
  N6: 5V->12V.Positive_Input, 5V.V+
  N7: 5V->12V.Negative_Output, water_pump.pin_2, F1.GND
  N8: 5V->12V.Positive_Output, water_pump.pin_1, F1.Power

custom parts:
  Bluetooth HC-06u: Bluetooth HC-06 - face up, pins down 16.5mm x 37.5mm PCB
  Boost Convertor: DC to DC boost convertor
  water pump/motor: WATER PUMP BY ARDUBLOCKTR
  Fan - 4 wire: Fan, 4 wire with tach.
